# Fritzing sketch uncloud (saved by Fritzing 0.9.2b)
breadboards: 1

parts:
  J1 = Screw terminal - 2 pins [package=THT]
  J2 = Screw terminal - 2 pins [package=THT]
  J4 = Screw terminal - 2 pins [package=THT]
  J5 = Screw terminal - 2 pins [package=THT]
  SLA_Battery = DC Power [voltage=12V]
  Fuse = Fuse with Handler [part_number=Htc-15m]
  J3 = screw terminal, 2 pins
  Yocto-Amp = Amperemeter
  Yocto-Volt = Voltmeter
  CONN1 = USB connector [package=THT]
  CONN2 = USB connector [package=THT]
  CONN3 = USB connector [package=THT]
  CONN4 = USB connector [package=THT]
  Power_plug1 = Power plug

nets:
  N1: J1.pin1, Yocto-Volt.Positive, Power_plug1.GND
  N2: J1.pin2, J4.pin1
  N3: J2.pin1, Yocto-Volt.Com, Power_plug1.VCC
  N4: J2.pin2, Yocto-Amp.Positive
  N5: J4.pin2, Fuse.Connector1
  N6: J5.pin1, J3.pin2
  N7: J5.pin2, SLA_Battery.V+
  N8: SLA_Battery.V-, Fuse.Connector2
  N9: J3.pin1, Yocto-Amp.Com
  5V: CONN1.5V, CONN4.5V
  N10: CONN1.d-, CONN4.d-
  N11: CONN1.d+, CONN4.d+
  GND: CONN1.GND, CONN1.chassis6, CONN4.GND, CONN4.chassis6
  5V_2: CONN2.5V, CONN3.5V
  N12: CONN2.d-, CONN3.d-
  N13: CONN2.d+, CONN3.d+
  GND_2: CONN2.GND, CONN3.GND, CONN3.chassis6

notes:
  NUC
  unCloud, Providing computing services without a consistent power or world wide web connection, 1.1

custom parts:
  Amperemeter: A Standard Multimeter in Current mode
  Voltmeter: A Standard Multimeter in Current mode
